# Fritzing sketch zapojeni (saved by Fritzing 0.9.3b)

parts:
  OLED1 = OLED 128x64 I2C Monochrome Display
  LED1 = smd LED [color="Red (633nm)" package="0805 [SMD]"]
  Součástka1 = Passive Buzzer
  U1 = NodeMCU V3.0

nets:
  GND: OLED1.GND, LED1.cathode, Součástka1.GND, U1.GND
  VDD: OLED1.VDD, U1.3V3
  N1: OLED1.SCK, U1.D1
  N2: OLED1.SDA, U1.D2
  N3: LED1.anode, U1.D7
  N4: Součástka1.S, U1.D5

custom parts:
  NodeMCU V3.0: ESP8266 based NodeMCU
